# Fritzing sketch Project_final (saved by Fritzing 0.9.3b)
breadboards: 1

parts:
  Part1 = Arduino Uno (Rev3) - ICSP
  M1 = fc-51 [package=THT]
  J1 = Piezo Speaker
  LED1 = smd LED [color="Green (570nm)" package="1206 [SMD]"]
  LED2 = smd LED [color="Red (633nm)" package="1206 [SMD]"]
  Part2 = RFID-RC522-v2
  LED3 = smd LED [color="Blue (470nm)" package="1206 [SMD]"]
  J2 = Basic Servo
  LED4 = smd LED [color="Blue (470nm)" package="1206 [SMD]"]
  M2 = fc-51 [package=THT]

nets:
  N1: Part1.A0, M2.pin1
  N2: Part1.A1, M1.pin1
  N3: Part1.D8, LED4.anode
  N4: Part1.D9_PWM, Part2.RST
  N5: Part1.D10_PWM/SS, Part2.SDA
  N6: Part1.D11_PWM/MOSI, Part2.MOSI
  N7: Part1.D12/MISO, Part2.MISO
  N8: Part1.D13/SCK, Part2.SCK
  GND: Part1.GND, M1.pin2, Part2.GND, J2.gnd, LED4.cathode, M2.pin2
  N9: Part1.D2, J1.pin2
  N10: Part1.D3_PWM, J2.pulse
  N11: Part1.D4, LED1.anode
  N12: Part1.D5_PWM, LED2.anode
  N13: Part1.D7, LED3.anode
  3V3: Part1.3V3, M1.pin3, Part2.3.3V, M2.pin3
  5V: Part1.5V, J2.vcc

notes:
  VIP CAR PARKING SYSTEM

custom parts:
  RFID-RC522-v2: A simple China made RFID-RC522 Reader; do check the pin labels, as this is a MFRC522 based clone.
